// Logisim project Lab1_P3_WaterTank.circ as structural Verilog: 1 circuit, main circuit main
module main (
  input  Full_level__F,
  input  Mid_level__M,
  input  Pressure__P,
  input  Opacity__C,
  input  PH_level__H,
  output Blue,
  output Red,
  output Green,
  output Blue_2
);

  wire _1_2_out, _1_out, _2_out, _3_2_out, _3_out, _4_2_out, _4_out;

  and _1 (_1_out, Mid_level__M, Pressure__P);
  and _1_2 (_1_2_out, Mid_level__M, Opacity__C);
  or _2 (_2_out, Pressure__P, Opacity__C, PH_level__H);
  or _3 (_3_out, PH_level__H, Pressure__P);
  or _3_2 (_3_2_out, Mid_level__M, Full_level__F);
  and _4 (_4_out, Pressure__P, Opacity__C);
  or _4_2 (_4_2_out, Mid_level__M, Full_level__F);
  or _1_3 (Blue, _1_out, _1_2_out);
  and _2_2 (Red, Mid_level__M, _2_out);
  and _3_3 (Green, _3_out, _3_2_out);
  and _4_3 (Blue_2, _4_out, _4_2_out);
endmodule
