// Logisim project Lab2_P1_CarSecuritySystem.circ as structural Verilog: 1 circuit, main circuit main
module main (
  input  K,
  input  C,
  input  S,
  output B,
  output E
);

  wire and_1_out, nand_1_out;

  nand nand_1 (nand_1_out, C, S);
  and and_1 (and_1_out, K, C);
  and and_2 (B, K, nand_1_out);
  and and_3 (E, and_1_out, S);
endmodule
