// Logisim project Lab3_P2_HecDecode.circ as structural Verilog: 1 circuit, main circuit main
module main (
  input  A,
  input  B,
  input  C,
  input  D
);

  wire A_B_C_D_prime_out, A_B_prime_C_out, A_B_prime_D_out, a_out, A_prime_B_out,
       A_prime_B_prime_D_prime_out, A_prime_B_prime_out, A_prime_BC_prime_out, A_prime_BD_out, A_prime_C_out,
       A_prime_C_prime_D_prime_out, A_prime_C_prime_out, A_prime_CD_out, A_prime_D_out, AB_prime_C_prime_out,
       AB_prime_out, AC_prime_D_out, AC_prime_out, AD_prime_out, B_C_D_prime_out, B_C_prime_out, b_out,
       B_prime_C_D_prime_out, B_prime_C_out, B_prime_CD_out, B_prime_D_out, B_prime_D_prime_2_out,
       B_prime_D_prime_out, BC_out, BC_prime_D_out, BCD_prime_out, C_B_prime_D_prime_out, c_out,
       C_prime_D_out, D__B_C_prime_out, d_out, e_out, f_out, g_out, not_1_out, not_2_out, not_3_out,
       not_4_out;

  not not_1 (not_1_out, A);
  not not_2 (not_2_out, C);
  not not_3 (not_3_out, B);
  not not_4 (not_4_out, D);
  and B_prime_D_prime (B_prime_D_prime_out, not_3_out, not_4_out);
  and A_prime_C (A_prime_C_out, not_1_out, C);
  and BC (BC_out, B, C);
  and AD_prime (AD_prime_out, A, not_4_out);
  and A_prime_BD (A_prime_BD_out, not_1_out, B, D);
  and AB_prime_C_prime (AB_prime_C_prime_out, A, not_3_out, not_2_out);
  and A_prime_B_prime (A_prime_B_prime_out, not_1_out, not_3_out);
  and A_prime_C_prime_D_prime (A_prime_C_prime_D_prime_out, not_1_out, not_2_out, not_4_out);
  and AC_prime_D (AC_prime_D_out, A, not_2_out, D);
  and A_prime_CD (A_prime_CD_out, not_1_out, C, D);
  and C_prime_D (C_prime_D_out, not_2_out, D);
  and AB_prime (AB_prime_out, A, not_3_out);
  and A_prime_B (A_prime_B_out, not_1_out, B);
  and A_prime_C_prime (A_prime_C_prime_out, not_1_out, not_2_out);
  and A_prime_D (A_prime_D_out, not_1_out, D);
  and A_prime_B_prime_D_prime (A_prime_B_prime_D_prime_out, not_1_out, not_3_out, not_4_out);
  and B_prime_CD (B_prime_CD_out, not_3_out, C, D);
  and BC_prime_D (BC_prime_D_out, B, not_2_out, D);
  and BCD_prime (BCD_prime_out, B, C, not_4_out);
  and AC_prime (AC_prime_out, A, not_2_out);
  or u_a (a_out, B_prime_D_prime_out, A_prime_C_out, BC_out, AD_prime_out, A_prime_BD_out, AB_prime_C_prime_out);
  or u_b (b_out, B_prime_D_prime_out, A_prime_B_prime_out, A_prime_C_prime_D_prime_out, AC_prime_D_out, A_prime_CD_out);
  or u_c (c_out, C_prime_D_out, AB_prime_out, A_prime_B_out, A_prime_C_prime_out, A_prime_D_out);
  or u_d (d_out, A_prime_B_prime_D_prime_out, B_prime_CD_out, BC_prime_D_out, BCD_prime_out, AC_prime_out);
  _7_Segment_Display u_7_segment_display_1 (
    .g(g_out), .f(f_out), .a(a_out), .b(b_out), .e(e_out), .d(d_out), .c(c_out));  // open: dp
  or e (e_out, B_prime_C_D_prime_out, A_B_C_D_prime_out);
  or f (f_out, A_B_prime_C_out, D__B_C_prime_out, A_prime_BC_prime_out);
  or g (g_out, A_prime_BC_prime_out, A_B_prime_D_out, C_B_prime_D_prime_out);
  and B_prime_C_D_prime (B_prime_C_D_prime_out, B_prime_C_out, not_4_out);
  and A_B_C_D_prime (A_B_C_D_prime_out, A, B_C_D_prime_out);
  and A_B_prime_C (A_B_prime_C_out, B_prime_C_out, A);
  and D__B_C_prime (D__B_C_prime_out, B_C_prime_out, not_4_out);
  and A_B_prime_D (A_B_prime_D_out, A, B_prime_D_out);
  and C_B_prime_D_prime (C_B_prime_D_prime_out, C, B_prime_D_prime_2_out);
  or B_prime_C (B_prime_C_out, not_3_out, C);
  or B_C_D_prime (B_C_D_prime_out, B, C, not_4_out);
  or B_C_prime (B_C_prime_out, B, not_2_out);
  and A_prime_BC_prime (A_prime_BC_prime_out, not_1_out, B, not_2_out);
  or B_prime_D (B_prime_D_out, not_3_out, D);
  or B_prime_D_prime_2 (B_prime_D_prime_2_out, not_3_out, not_4_out);

  // Notes on the sheet:
  //   A
  //   B
  //   -A
  //   -B
  //   -C
  //   C
  //   D
  //   -D
  //   c
  //   a
  //   f
  //   g
  //   d
  //   b
  //   e
  //   -D
  //   D
  //   -D
  //   C
  //   D
  //   -C
  //   C
  //   -C
  //   B
  //   A
  //   -A
  //   -B
  //   B
  //   A
  //   -A
  //   -B
endmodule
