// Logisim project Lab3_P3_CPE.circ as structural Verilog: 2 circuits, main circuit main
module main (
  input  B1,
  input  C1,
  input  B2,
  input  C2,
  input  B3,
  input  C3
);

  wire cpe_1_a, cpe_1_b_2, cpe_1_c_2, cpe_1_d, cpe_1_e, cpe_1_f, cpe_1_g, cpe_2_a, cpe_2_b_2, cpe_2_c_2,
       cpe_2_d, cpe_2_e, cpe_2_f, cpe_2_g, cpe_3_a, cpe_3_b_2, cpe_3_c_2, cpe_3_d, cpe_3_e, cpe_3_f, cpe_3_g;

  CPE cpe_1 (
    .B(B1), .C(C1), .a(cpe_1_a), .b_2(cpe_1_b_2), .c_2(cpe_1_c_2), .d(cpe_1_d), .e(cpe_1_e), .f(cpe_1_f),
    .g(cpe_1_g));
  CPE cpe_2 (
    .B(B2), .C(C2), .a(cpe_2_a), .b_2(cpe_2_b_2), .c_2(cpe_2_c_2), .d(cpe_2_d), .e(cpe_2_e), .f(cpe_2_f),
    .g(cpe_2_g));
  CPE cpe_3 (
    .B(B3), .C(C3), .a(cpe_3_a), .b_2(cpe_3_b_2), .c_2(cpe_3_c_2), .d(cpe_3_d), .e(cpe_3_e), .f(cpe_3_f),
    .g(cpe_3_g));
  _7_Segment_Display u_7_segment_display_1 (
    .g(cpe_1_g), .f(cpe_1_f), .a(cpe_1_a), .b(cpe_1_b_2), .e(cpe_1_e), .d(cpe_1_d), .c(cpe_1_c_2));  // open: dp
  _7_Segment_Display u_7_segment_display_2 (
    .g(cpe_2_g), .f(cpe_2_f), .a(cpe_2_a), .b(cpe_2_b_2), .e(cpe_2_e), .d(cpe_2_d), .c(cpe_2_c_2));  // open: dp
  _7_Segment_Display u_7_segment_display_3 (
    .g(cpe_3_g), .f(cpe_3_f), .a(cpe_3_a), .b(cpe_3_b_2), .e(cpe_3_e), .d(cpe_3_d), .c(cpe_3_c_2));  // open: dp
endmodule

module CPE (
  input  B,
  input  C,
  output a,
  output b_2,
  output c_2,
  output d,
  output e,
  output f,
  output g
);

  wire not_1_out, not_2_out;

  not not_1 (not_1_out, C);
  not not_2 (not_2_out, B);
  or B_C (a, B, C);
  and BC_prime (b_2, B, not_1_out);
  and _0 (c_2, B, not_2_out);

  assign d = C;
  assign e = a;
  assign f = a;
  assign g = B;
endmodule
