// Logisim project 2018_4.circ as structural Verilog: 1 circuit, main circuit main
module main (
  input  in_1,
  input  in_2,
  input  in_3,
  input  in_4,
  input  in_5,
  input  in_6,
  input  in_7,
  input  in_8,
  input  in_9,
  input  in_10,
  input  in_11,
  input  in_12,
  input  in_13,
  input  in_14,
  input  in_15,
  input  in_16,
  input  in_17,
  output F
);

  wire decoder_1_out0, decoder_1_out2, decoder_1_out3, decoder_1_out4, decoder_1_out5, decoder_1_out7,
       decoder_1_out9, decoder_1_out11, decoder_1_out12, decoder_1_out13, decoder_1_out15;
  wire [3:0] priority_encoder_1_out;

  Priority_Encoder #(.select(4)) priority_encoder_1 (
    .in0(in_1), .in1(in_2), .in2(in_3), .in3(in_4), .in4(in_5), .in5(in_6), .in6(in_7), .in7(in_8),
    .in8(in_10), .in9(in_11), .in10(in_12), .in11(in_13), .in12(in_14), .in13(in_15), .in14(in_16),
    .in15(in_17), .out(priority_encoder_1_out), .en_in(in_9));  // open: gs, en_out
  Decoder #(.select(4)) decoder_1 (
    .out0(decoder_1_out0), .out2(decoder_1_out2), .out3(decoder_1_out3), .out4(decoder_1_out4),
    .out5(decoder_1_out5), .out7(decoder_1_out7), .out9(decoder_1_out9), .out11(decoder_1_out11),
    .out12(decoder_1_out12), .out13(decoder_1_out13), .out15(decoder_1_out15), .sel(priority_encoder_1_out),
    .en(in_9));  // open: out1, out6, out8, out10, out14
  or or_1 (F, decoder_1_out0, decoder_1_out2, decoder_1_out3, decoder_1_out4, decoder_1_out5, decoder_1_out7, decoder_1_out9, decoder_1_out11, decoder_1_out12, decoder_1_out13, decoder_1_out15);
endmodule
