// Logisim project 2558_2_3.circ as structural Verilog: 1 circuit, main circuit main
module main (
  input  A,
  input  B,
  input  C,
  input  D,
  output F,
  output T
);

  wire nand_1_out, nand_2_out, nand_3_out, nand_4_out, nand_5_out, not_1_out, not_2_out, not_3_out, not_4_out;

  not not_1 (not_1_out, B);
  not not_2 (not_2_out, A);
  not not_3 (not_3_out, C);
  not not_4 (not_4_out, D);
  nand nand_1 (nand_1_out, A, not_1_out);
  nand nand_2 (nand_2_out, B, C);
  nand nand_3 (nand_3_out, not_1_out, D);
  nand nand_4 (nand_4_out, B, nand_2_out);
  nand nand_5 (nand_5_out, nand_2_out, C);
  nand nand_6 (T, not_2_out, nand_4_out, nand_5_out);
  nand nand_7 (F, nand_1_out, T, nand_3_out);
endmodule
