// Logisim project Lab1_P1.circ as structural Verilog: 1 circuit, main circuit main
module main (
  input  A,
  input  B,
  output LED1,
  output LED2
);

  wire not_1_out, not_2_out, not_3_out, not_4_out, not_5_out, not_6_out, not_7_out, U3_out, U4_out, U5_out,
       U6_out, U7_out, U8_out, U9_out, U10_out, U11_out;

  and U3 (U3_out, A, B);
  and U11 (U11_out, A, A);
  not not_1 (not_1_out, U3_out);
  not not_2 (not_2_out, U11_out);
  and U5 (U5_out, A, not_1_out);
  and U4 (U4_out, not_1_out, B);
  and U8 (U8_out, not_2_out, B);
  and U9 (U9_out, A, B);
  not not_3 (not_3_out, U5_out);
  not not_4 (not_4_out, U4_out);
  not not_5 (not_5_out, U8_out);
  not not_6 (not_6_out, U9_out);
  not not_7 (not_7_out, U6_out);
  and U6 (U6_out, not_3_out, not_4_out);
  not not_8 (LED2, U10_out);
  and U10 (U10_out, not_5_out, not_6_out);
  and U7 (U7_out, not_7_out, not_7_out);
  not not_9 (LED1, U7_out);
endmodule
