// Logisim project Lab1_P2.circ as structural Verilog: 1 circuit, main circuit main
module main (
  input  A,
  input  B,
  output LED1,
  output LED2
);

  wire U1_out, U2_out, U3_out, U5_out, U6_out, U7_out, U8_out, U9_out;

  nor U1 (U1_out, A, B);
  nor U6 (U6_out, B, B);
  nor U7 (U7_out, A, A);
  nor U2 (U2_out, A, U1_out);
  nor U3 (U3_out, U1_out, B);
  nor U5 (U5_out, A, U6_out);
  nor U8 (U8_out, U6_out, U7_out);
  nor U4 (LED1, U2_out, U3_out);
  nor U9 (U9_out, U5_out, U8_out);
  nor U10 (LED2, U9_out, U9_out);
endmodule
