// Logisim project Lab3_P1_BicycleLED.circ as structural Verilog: 1 circuit, main circuit main
module main (
  input  A,
  input  B,
  input  C,
  output L5,
  output L4,
  output L3,
  output L2,
  output L1
);

  wire A_prime_B_out, B_C_out, BC_out, not_1_out;

  not not_1 (not_1_out, A);
  and BC (BC_out, B, C);
  and A_prime_B (A_prime_B_out, B, not_1_out);
  or B_C (B_C_out, B, C);
  and A_B_C (L5, A, B_C_out);
  or A___BC (L3, BC_out, A);
  or A_prime_B___A (L2, A_prime_B_out, A);
  or A__B_C (L1, A, B_C_out);

  assign L4 = A;

  // Notes on the sheet:
  //   C
  //   C
  //   A
  //   B
  //   A
  //   B
endmodule
