// Logisim project Lab4_P3_StringCompare.circ as structural Verilog: 1 circuit, main circuit main
module main (
  input  B0,
  input  B1,
  input  B2,
  input  B3,
  input  A0,
  input  A1,
  input  A2,
  input  A3,
  output _1__Same,
  output _2__Not_same
);

  wire xor_1_out, xor_2_out, xor_3_out, xor_4_out;

  xor xor_1 (xor_1_out, A0, B0);
  xor xor_2 (xor_2_out, A1, B1);
  xor xor_3 (xor_3_out, A2, B2);
  xor xor_4 (xor_4_out, A3, B3);
  or or_1 (_2__Not_same, xor_1_out, xor_2_out, xor_3_out, xor_4_out);
  not not_1 (_1__Same, _2__Not_same);
endmodule
