// Logisim project lab4_P1_Mux.circ as structural Verilog: 1 circuit, main circuit main
module main (
  input  in_1,
  input  A,
  input  B,
  output out_4
);

  wire _00_out, _01_out, _10_out, _11_out, not_1_out, not_2_out, not_3_out, not_4_out, or_1_out;

  or or_1 (or_1_out, in_1, not_1_out);
  not not_1 (not_1_out, in_1);
  not not_2 (not_2_out, or_1_out);
  not not_3 (not_3_out, A);
  not not_4 (not_4_out, B);
  and _00 (_00_out, not_2_out, not_3_out, not_4_out);
  and _01 (_01_out, or_1_out, not_3_out, B);
  and _10 (_10_out, or_1_out, A, not_4_out);
  and _11 (_11_out, not_2_out, A, B);
  or or_2 (out_4, _00_out, _01_out, _10_out, _11_out);

  // Notes on the sheet:
  //   True
  //   False
  //   01
  //   00
  //   10
  //   11
endmodule
