// Logisim project Lab5_P1_StateABCD.circ as structural Verilog: 1 circuit, main circuit main
module main (
);

  wire and_1_out, and_2_out, and_3_out, clock_1_out, D0_q, D1_q, D1_qn, D2_qn, or_1_out;

  Clock clock_1 (.out(clock_1_out));
  and and_1 (and_1_out, D0_q, D1_q);
  D_Flip_Flop D2 (.clk(clock_1_out), .D(and_1_out), .Qn(D2_qn));  // open: Q, preset, en, reset
  D_Flip_Flop D1 (.clk(clock_1_out), .D(D1_qn), .Q(D1_q), .Qn(D1_qn));  // open: preset, en, reset
  D_Flip_Flop D0 (.clk(clock_1_out), .D(or_1_out), .Q(D0_q));  // open: Qn, preset, en, reset
  and and_2 (and_2_out, D1_qn, D2_qn);
  and and_3 (and_3_out, D0_q, D2_qn);
  or or_1 (or_1_out, and_2_out, and_3_out);
endmodule
