// Logisim project Lab5_P2_lift.circ as structural Verilog: 1 circuit, main circuit main
module main (
  input  in_1,
  output Current_State,
  output Output
);

  wire clock_1_out;

  T_Flip_Flop t_ff_1 (.clk(clock_1_out), .T(in_1), .Q(Current_State));  // open: Qn, preset, reset, en
  Clock clock_1 (.out(clock_1_out));

  assign Output = Current_State;
endmodule
