// Logisim project Lab5_P3_SinglePluse.circ as structural Verilog: 1 circuit, main circuit main
module main (
);

  wire A_B_out, A_prime_B_prime_out, A_q, A_qn, B_q, B_qn, button_1_out, clock_1_out, I_A_B_out;

  Button button_1 (.out(button_1_out));
  Clock clock_1 (.out(clock_1_out));
  and I_A_B (I_A_B_out, button_1_out, A_B_out);
  or A_B (A_B_out, A_q, B_q);
  and A_prime_B_prime (A_prime_B_prime_out, B_qn, A_qn, button_1_out);
  D_Flip_Flop A (.clk(clock_1_out), .D(I_A_B_out), .Q(A_q), .Qn(A_qn));  // open: preset, en, reset
  D_Flip_Flop B (.clk(clock_1_out), .D(A_prime_B_prime_out), .Q(B_q), .Qn(B_qn));  // open: preset, en, reset
  LED led_1 (.in(B_q));

  // Notes on the sheet:
  //   I
endmodule
