// Logisim project CPE_7Seg.circ as structural Verilog: 1 circuit, main circuit main
module main (
  input  in_1
);

  wire _0_out, B_C_out, BC_prime_out, clock_1_out, D1_2_q, D1_out, D2_2_q, D2_2_qn, D2_out, not_1_out,
       not_2_out, Q1_Q2_out;

  Clock clock_1 (.out(clock_1_out));
  xor Q1_Q2 (Q1_Q2_out, D1_2_q, D2_2_q);
  and D1 (D1_out, Q1_Q2_out, in_1);
  and D2 (D2_out, in_1, D2_2_qn);
  D_Flip_Flop D1_2 (.clk(clock_1_out), .D(D1_out), .Q(D1_2_q));  // open: Qn, preset, en, reset
  D_Flip_Flop D2_2 (.clk(clock_1_out), .D(D2_out), .Q(D2_2_q), .Qn(D2_2_qn));  // open: preset, en, reset
  not not_1 (not_1_out, D2_2_q);
  not not_2 (not_2_out, D1_2_q);
  or B_C (B_C_out, D1_2_q, D2_2_q);
  and BC_prime (BC_prime_out, D1_2_q, not_1_out);
  and _0 (_0_out, D1_2_q, not_2_out);
  _7_Segment_Display u_7_segment_display_1 (
    .g(D1_2_q), .f(B_C_out), .a(B_C_out), .b(BC_prime_out), .e(B_C_out), .d(D2_2_q), .c(_0_out));  // open: dp
endmodule
