// Logisim project Lab6_P1_FordThunderbird.circ as structural Verilog: 1 circuit, main circuit main
module main (
  input  L,
  input  R,
  input  H,
  output out_4,
  output out_5,
  output out_6,
  output out_7,
  output out_8,
  output out_9
);

  wire clock_1_out, D1_out, D2_out, d_ff_1_q, d_ff_1_qn, d_ff_2_q, d_ff_2_qn, HQ2_out, I_out,
       Q1_prime_Q2I_out, Q1_Q2_L_out, Q1_Q2_out, Q1_Q2_R_out, Q1L_out, Q1Q2_prime_I_out, Q1Q2L_out,
       Q1Q2R_out, Q1R_out;

  or I (I_out, L, H, R);
  and HQ2 (HQ2_out, d_ff_2_q, H);
  or LC (out_4, HQ2_out, Q1Q2L_out);
  and Q1Q2L (Q1Q2L_out, d_ff_1_q, d_ff_2_q, L);
  and Q1Q2_prime_I (Q1Q2_prime_I_out, I_out, d_ff_2_qn, d_ff_1_q);
  and Q1_prime_Q2I (Q1_prime_Q2I_out, I_out, d_ff_1_qn, d_ff_2_q);
  and Q1L (Q1L_out, d_ff_1_q, L);
  or LB (out_5, HQ2_out, Q1L_out);
  Clock clock_1 (.out(clock_1_out));
  or D1 (D1_out, Q1Q2_prime_I_out, Q1_prime_Q2I_out);
  and D2 (D2_out, I_out, d_ff_2_qn);
  and Q1_Q2_L (Q1_Q2_L_out, L, Q1_Q2_out);
  or LA (out_6, HQ2_out, Q1_Q2_L_out);
  D_Flip_Flop d_ff_1 (.clk(clock_1_out), .D(D1_out), .Q(d_ff_1_q), .Qn(d_ff_1_qn));  // open: preset, en, reset
  D_Flip_Flop d_ff_2 (.clk(clock_1_out), .D(D2_out), .Q(d_ff_2_q), .Qn(d_ff_2_qn));  // open: preset, en, reset
  or Q1_Q2 (Q1_Q2_out, d_ff_2_q, d_ff_1_q);
  and Q1_Q2_R (Q1_Q2_R_out, Q1_Q2_out, R);
  or RA (out_7, HQ2_out, Q1_Q2_R_out);
  and Q1R (Q1R_out, d_ff_1_q, R);
  or RB (out_8, HQ2_out, Q1R_out);
  or RC (out_9, HQ2_out, Q1Q2R_out);
  // XOR_Gate xor_1 is placed but not wired
  and Q1Q2R (Q1Q2R_out, d_ff_1_q, d_ff_2_q, R);

  // Notes on the sheet:
  //   Q1
  //   Q2
  //   R
  //   L
  //   Q1
  //   Q2
  //   R
endmodule
